// Logisim project Cache.circ as structural Verilog: 3 circuits, main circuit Cache
module Cache (
  input  clk,
  input  rst_n,
  input  [1:0] byte_size,
  input  [31:0] wdata,
  input  [31:0] rdata,
  input  [31:0] ldata,
  input  [31:0] write_back_data,
  input  write_enable,
  input  read_enable,
  input  [31:0] addr,
  input  write_back_finished,
  output write_back_enable,
  output op_finished,
  output hit,
  output dirty
);

  wire set_1_load_enable;
  wire [1:0] set_1_cs, way_2_dirty_way, way_2_hit_way, way_2_valid_way;

  Way way_1 (
    .clk(clk), .rst_n(rst_n), .cs(set_1_cs[1]), .addr(addr), .wdata(wdata), .ldata(ldata),
    .write_enable(write_enable), .load_enable(set_1_load_enable), .byte_size(byte_size), .rdata(rdata),
    .write_back_data(write_back_data), .hit_way(way_2_hit_way[1]), .dirty_way(way_2_dirty_way[1]),
    .valid_way(way_2_valid_way[1]), .read_enable(read_enable));
  Set set_1 (
    .dirty_status(way_2_hit_way), .hit_status(way_2_dirty_way), .cs(set_1_cs),
    .valid_status(way_2_valid_way), .addr(addr), .write_enable(write_enable),
    .load_enable(set_1_load_enable), .read_enable(read_enable), .rst_n(clk), .clk(rst_n),
    .write_back_enable(write_back_enable), .write_back_finished(write_back_finished),
    .op_finished(op_finished), .hit(hit), .dirty(dirty));
  Way way_2 (
    .clk(clk), .rst_n(rst_n), .cs(set_1_cs[0]), .addr(addr), .wdata(wdata), .ldata(ldata),
    .write_enable(write_enable), .load_enable(set_1_load_enable), .byte_size(byte_size), .rdata(rdata),
    .write_back_data(write_back_data), .hit_way(way_2_hit_way[0]), .dirty_way(way_2_dirty_way[0]),
    .valid_way(way_2_valid_way[0]), .read_enable(read_enable));
endmodule

module Way (
  input  clk,
  input  rst_n,
  input  cs,
  input  [31:0] addr,
  input  read_enable,
  input  [31:0] wdata,
  input  [31:0] ldata,
  input  write_enable,
  input  load_enable,
  input  [1:0] byte_size,
  output [31:0] rdata,
  output [31:0] write_back_data,
  output hit_way,
  output dirty_way,
  output valid_way
);
endmodule

module Set (
  input  [31:0] addr,
  input  clk,
  input  rst_n,
  input  [1:0] dirty_status,
  input  write_back_finished,
  input  [1:0] hit_status,
  input  [1:0] valid_status,
  input  write_enable,
  input  read_enable,
  output [1:0] cs,
  output load_enable,
  output write_back_enable,
  output op_finished,
  output hit,
  output dirty
);
endmodule
